# Fritzing sketch schematic (saved by Fritzing 0.9.3b)

parts:
  J1 = STM32 Nucleo boards
  Part1 = Barometric Pressure Sensor - BMP180 Breakout (GY-68)

nets:
  N1: J1.A4/SDA, Part1.SDA
  N2: J1.A5/SCL, Part1.SCL
  3V3: J1.3V3, Part1.VCC
  GND: J1.GND, Part1.GND
