# Fritzing sketch schematic (saved by Fritzing 0.9.3b)

parts:
  J1 = STM32 Nucleo boards
  R1 = Trimmer Potentiometer [maximum_resistance=10kΩ package=THT]

nets:
  N1: J1.A0, R1.wiper
  N2: J1.3V3, R1.leg2
  N3: J1.GND, R1.leg1
