# Fritzing sketch schematic (saved by Fritzing 0.9.3b)

parts:
  J1 = STM32 Nucleo boards
  ZS-042_RTC1 = ZS-042 RTC Module

nets:
  N1: J1.A4/SDA, ZS-042_RTC1.SDA
  N2: J1.A5/SCL, ZS-042_RTC1.SCL
  5V: J1.5V, ZS-042_RTC1.VCC
  GND: J1.GND, ZS-042_RTC1.GND
