# Fritzing sketch schematic (saved by Fritzing 0.9.3b)

parts:
  J1 = STM32 Nucleo boards
  Part1 = LCD1602-I2C

nets:
  N1: J1.A4/SDA, Part1.SDA
  N2: J1.A5/SCL, Part1.SCL
  5V: J1.5V, Part1.VCC
  GND: J1.GND, Part1.GND

custom parts:
  LCD1602-I2C: A standard character display, usually with 2x16 characters. Comes in many colors with LCM1602 IIC attached.
